# Fritzing sketch Aufbau (saved by Fritzing 0.9.3b)
breadboards: 1

parts:
  Bauteil1 = Arduino Uno (Rev3) - ICSP
  J1 = Basic Servo
  Bauteil2 = ws2812b [package="smd 2812b"]
  Bauteil3 = ws2812b [package="smd 2812b"]
  ULN1 = Darlington Driver [package=dil18]
  LED1 = smd LED [color="Red (633nm)" package="1206 [SMD]"]
  LED2 = smd LED [color="Red (633nm)" package="1206 [SMD]"]

nets:
  N1: Bauteil1.D8, J1.pulse
  N2: Bauteil1.D9_PWM, Bauteil2.DIN
  N3: Bauteil1.D10_PWM/SS, LED2.anode
  N4: Bauteil1.D13/SCK, ULN1.18
  GND: Bauteil1.GND, J1.gnd, Bauteil2.VSS, Bauteil3.VSS, ULN1.9, LED2.cathode
  VDD: Bauteil1.5V, J1.vcc, Bauteil2.VDD, Bauteil3.VDD
  N5: Bauteil1.VIN, ULN1.10, LED1.anode
  N6: Bauteil2.DOUT, Bauteil3.DIN
  N7: ULN1.1, LED1.cathode

notes:
  Rauchgenerator (12V)
  AlarmLED (5V)
  I2C Kommunikation mit Taster Arduino
