# Fritzing sketch Aufbau (saved by Fritzing 0.9.3b)
breadboards: 1

parts:
  Bauteil1 = Arduino Uno (Rev3)
  ULN1 = Darlington Driver [package=dil18]
  Bauteil2 = ws2812b [package="smd 2812b"]
  Bauteil3 = ws2812b [package="smd 2812b"]
  Bauteil4 = ws2812b [package="smd 2812b"]
  Bauteil5 = ws2812b [package="smd 2812b"]
  LED1 = LED - 5mm [color="Red (633nm)" package="5 mm [THT]"]
  LED2 = LED - 5mm [color="Red (633nm)" package="5 mm [THT]"]

nets:
  N1: Bauteil1.D11_PWM/MOSI, Bauteil3.DIN
  N2: Bauteil1.GND, ULN1.9
  N3: Bauteil1.VIN, ULN1.10, LED1.anode, LED2.anode
  N4: ULN1.1, LED2.cathode
  N5: ULN1.2, LED1.cathode
  VDD: Bauteil2.VDD, Bauteil3.VDD, Bauteil4.VDD, Bauteil5.VDD
  N6: Bauteil2.DOUT, Bauteil4.DIN
  VSS: Bauteil2.VSS, Bauteil3.VSS, Bauteil4.VSS, Bauteil5.VSS
  N7: Bauteil2.DIN, Bauteil3.DOUT
  N8: Bauteil4.DOUT, Bauteil5.DIN

notes:
  I2C-Kommunikation mit dem Arduino für die Taster
  Feuerkorb Modul (12V)
  Bleuchtung (12V)
