# Fritzing sketch Aufbau (saved by Fritzing 0.9.3b)
breadboards: 1

parts:
  Arduino_Mega = Arduino Mega 2560 (Rev3)
  S1 = Round Pushbutton
  S2 = Round Pushbutton
  S3 = Round Pushbutton
  S5 = Round Pushbutton
  S6 = Round Pushbutton
  LED1 = LED - 3mm [color="Red (633nm)" package="3 mm [THT]"]
  LED2 = LED - 3mm [color="Red (633nm)" package="3 mm [THT]"]
  LED3 = LED - 3mm [color="Red (633nm)" package="3 mm [THT]"]
  LED4 = LED - 3mm [color="Red (633nm)" package="3 mm [THT]"]
  LED5 = LED - 3mm [color="Red (633nm)" package="3 mm [THT]"]
  LED6 = LED - 3mm [color="Red (633nm)" package="3 mm [THT]"]
  ULN1 = Darlington Driver [package=dil18]
  S4 = Round Pushbutton
  R1 = Resistor [tolerance=±5% resistance=10k package=THT]
  R2 = Resistor [tolerance=±5% resistance=10k package=THT]

nets:
  N1: Arduino_Mega.SCL, R1.Pin_1
  N2: Arduino_Mega.SDA, R2.Pin_1
  N3: Arduino_Mega.GND, ULN1.9
  N4: Arduino_Mega.VIN, LED1.anode, LED2.anode, LED3.anode, LED4.anode, LED5.anode, LED6.anode, ULN1.10, R1.Pin_0, R2.Pin_0
  N5: Arduino_Mega.D2_PWM, S6.leg0
  N6: Arduino_Mega.D3_PWM, S5.leg0
  N7: Arduino_Mega.D4_PWM, S4.leg0
  N8: Arduino_Mega.D5_PWM, S3.leg0
  N9: Arduino_Mega.D6_PWM, S2.leg0
  N10: Arduino_Mega.D7_PWM, S1.leg0
  N11: Arduino_Mega.D34, ULN1.3
  N12: Arduino_Mega.D36, ULN1.4
  N13: Arduino_Mega.D38, ULN1.5
  N14: Arduino_Mega.D40, ULN1.6
  N15: Arduino_Mega.D42, ULN1.7
  N16: Arduino_Mega.D44, ULN1.8
  N17: S1.leg1, LED1.cathode, ULN1.11
  N18: S2.leg1, LED2.cathode, ULN1.12
  N19: S3.leg1, LED3.cathode, ULN1.13
  N20: S5.leg1, LED5.cathode, ULN1.15
  N21: S6.leg1, LED6.cathode, ULN1.16
  N22: LED4.cathode, ULN1.14, S4.leg1
